# Fritzing sketch Task1.1P (saved by Fritzing 0.9.3b)
circuit board: 8.46667cm x 5.64444cm
breadboards: 1

parts:
  R1 = Resistor [tolerance=±5% resistance=220 package=THT]
  LED1 = LED - 5mm [color="Red (633nm)" package="5 mm [THT]"]
  HCSR505_PIR = PIR_sensor
  Board = Arduino Uno (Rev3)

nets:
  N1: R1.Pin_0, Board.D13/SCK
  N2: R1.Pin_1, LED1.anode
  N3: LED1.cathode, HCSR505_PIR.connector3, Board.GND
  N4: HCSR505_PIR.connector1, Board.3V3
  N5: HCSR505_PIR.connector2, Board.D6_PWM
