# Fritzing sketch Task1.4D (saved by Fritzing 0.9.3b)
breadboards: 1

parts:
  R1 = Resistor [tolerance=±5% resistance=220 package=THT]
  LED1 = LED - 5mm [color="Red (633nm)" package="5 mm [THT]"]
  HCSR505_PIR_1 = PIR_sensor
  Board = Arduino Uno (Rev3)
  HCSR505_PIR_2 = PIR_sensor
  LED2 = LED - 5mm [color="Blue (430nm)" package="5 mm [THT]"]
  R2 = Resistor [tolerance=±5% resistance=220 package=THT]
  HCSR505_PIR_3 = PIR_sensor
  HCSR505_PIR_4 = PIR_sensor

nets:
  N1: R1.Pin_0, Board.D12/MISO
  N2: R1.Pin_1, LED1.anode
  N3: LED1.cathode, HCSR505_PIR_1.connector3, Board.GND, HCSR505_PIR_2.connector3, LED2.cathode, HCSR505_PIR_3.connector3, HCSR505_PIR_4.connector3
  N4: HCSR505_PIR_1.connector1, Board.5V, HCSR505_PIR_2.connector1, HCSR505_PIR_3.connector1, HCSR505_PIR_4.connector1
  N5: HCSR505_PIR_1.connector2, Board.D2
  N6: Board.D11_PWM/MOSI, R2.Pin_0
  N7: Board.D3_PWM, HCSR505_PIR_2.connector2
  N8: Board.D4, HCSR505_PIR_3.connector2
  N9: Board.D5_PWM, HCSR505_PIR_4.connector2
  N10: LED2.anode, R2.Pin_1
